// Logisim project Pattern_Detector.circ as structural Verilog: 1 circuit, main circuit main
module main (
  input  in_1,
  input  in_2,
  input  in_3,
  input  in_4,
  input  in_5,
  input  in_6,
  input  in_7,
  input  in_8,
  input  in_9,
  input  in_10,
  input  in_11,
  input  in_12,
  input  in_13,
  input  in_14,
  input  in_15,
  input  in_16,
  input  in_17,
  input  in_18,
  input  in_19,
  input  in_20,
  input  in_21,
  input  in_22,
  input  in_23,
  input  in_24,
  input  in_25,
  input  in_26,
  input  in_27,
  input  in_28,
  input  in_29,
  input  in_30,
  input  in_31,
  input  in_32,
  input  in_33,
  input  in_34,
  input  in_35,
  input  in_36,
  input  in_37,
  input  in_38,
  input  in_39,
  input  in_40,
  input  in_41,
  input  in_42,
  input  in_43,
  input  in_44,
  input  in_45,
  input  in_46,
  input  in_47,
  input  in_48
);

  wire and_1_out, and_2_out, and_3_out, and_4_out, and_5_out, and_6_out, and_7_out, and_8_out, and_9_out,
       and_10_out, and_11_out, and_12_out, and_13_out, and_14_out, and_15_out, and_16_out, and_17_out,
       and_18_out, and_19_out, and_20_out, and_21_out, and_22_out, and_23_out, and_24_out, and_25_out,
       and_26_out, and_27_out, and_28_out, and_29_out, and_30_out, and_31_out, and_32_out, and_33_out,
       and_34_out, and_35_out, and_36_out, and_37_out, and_38_out, not_1_out, not_2_out, xnor_1_out,
       xnor_2_out, xnor_3_out, xnor_4_out, xnor_5_out, xnor_6_out, xnor_7_out, xnor_8_out, xnor_9_out,
       xnor_10_out, xnor_11_out, xnor_12_out, xnor_13_out, xnor_14_out, xnor_15_out, xnor_16_out,
       xnor_17_out, xnor_18_out, xnor_19_out, xnor_20_out, xnor_21_out, xnor_22_out, xnor_23_out,
       xnor_24_out, xnor_25_out, xnor_26_out, xnor_27_out, xnor_28_out, xnor_29_out, xnor_30_out,
       xnor_31_out, xnor_32_out;

  LED led_1 (.in(in_17));
  LED led_2 (.in(in_18));
  LED led_3 (.in(in_21));
  LED led_4 (.in(in_22));
  LED led_5 (.in(in_25));
  LED led_6 (.in(in_26));
  LED led_7 (.in(in_29));
  LED led_8 (.in(in_30));
  LED led_9 (.in(in_17));
  LED led_10 (.in(in_18));
  LED led_11 (.in(in_21));
  LED led_12 (.in(in_22));
  LED led_13 (.in(in_25));
  LED led_14 (.in(in_26));
  LED led_15 (.in(in_29));
  LED led_16 (.in(in_30));
  LED led_17 (.in(in_19));
  LED led_18 (.in(in_23));
  LED led_19 (.in(in_27));
  LED led_20 (.in(in_31));
  LED led_21 (.in(in_19));
  LED led_22 (.in(in_23));
  LED led_23 (.in(in_27));
  LED led_24 (.in(in_31));
  LED led_25 (.in(in_20));
  LED led_26 (.in(in_24));
  LED led_27 (.in(in_28));
  LED led_28 (.in(in_32));
  LED led_29 (.in(in_20));
  LED led_30 (.in(in_24));
  LED led_31 (.in(in_28));
  LED led_32 (.in(in_32));
  and and_1 (and_1_out, in_17, in_1);
  and and_2 (and_2_out, in_21, in_5);
  and and_3 (and_3_out, in_25, in_9);
  and and_4 (and_4_out, in_29, in_13);
  and and_5 (and_5_out, in_17, in_33);
  and and_6 (and_6_out, in_21, in_37);
  and and_7 (and_7_out, in_25, in_41);
  and and_8 (and_8_out, in_29, in_45);
  and and_9 (and_9_out, in_18, in_2);
  and and_10 (and_10_out, in_22, in_6);
  and and_11 (and_11_out, in_26, in_10);
  and and_12 (and_12_out, in_30, in_14);
  and and_13 (and_13_out, in_18, in_34);
  and and_14 (and_14_out, in_22, in_38);
  and and_15 (and_15_out, in_26, in_42);
  and and_16 (and_16_out, in_30, in_46);
  and and_17 (and_17_out, in_19, in_3);
  and and_18 (and_18_out, in_23, in_7);
  and and_19 (and_19_out, in_27, in_11);
  and and_20 (and_20_out, in_31, in_15);
  and and_21 (and_21_out, in_19, in_35);
  and and_22 (and_22_out, in_23, in_39);
  and and_23 (and_23_out, in_27, in_43);
  and and_24 (and_24_out, in_31, in_47);
  and and_25 (and_25_out, in_20, in_4);
  and and_26 (and_26_out, in_24, in_8);
  and and_27 (and_27_out, in_28, in_12);
  and and_28 (and_28_out, in_32, in_16);
  and and_29 (and_29_out, in_20, in_36);
  and and_30 (and_30_out, in_24, in_40);
  and and_31 (and_31_out, in_28, in_44);
  and and_32 (and_32_out, in_32, in_48);
  LED led_33 (.in(and_1_out));
  LED led_34 (.in(and_9_out));
  LED led_35 (.in(and_2_out));
  LED led_36 (.in(and_10_out));
  LED led_37 (.in(and_3_out));
  LED led_38 (.in(and_11_out));
  LED led_39 (.in(and_4_out));
  LED led_40 (.in(and_12_out));
  LED led_41 (.in(and_5_out));
  LED led_42 (.in(and_13_out));
  LED led_43 (.in(and_6_out));
  LED led_44 (.in(and_14_out));
  LED led_45 (.in(and_7_out));
  LED led_46 (.in(and_15_out));
  LED led_47 (.in(and_8_out));
  LED led_48 (.in(and_16_out));
  LED led_49 (.in(and_17_out));
  LED led_50 (.in(and_18_out));
  LED led_51 (.in(and_19_out));
  LED led_52 (.in(and_20_out));
  LED led_53 (.in(and_21_out));
  LED led_54 (.in(and_22_out));
  LED led_55 (.in(and_23_out));
  LED led_56 (.in(and_24_out));
  LED led_57 (.in(and_25_out));
  LED led_58 (.in(and_26_out));
  LED led_59 (.in(and_27_out));
  LED led_60 (.in(and_28_out));
  LED led_61 (.in(and_29_out));
  LED led_62 (.in(and_30_out));
  LED led_63 (.in(and_31_out));
  LED led_64 (.in(and_32_out));
  xnor xnor_1 (xnor_1_out, and_1_out, in_17);
  xnor xnor_2 (xnor_2_out, and_2_out, in_21);
  xnor xnor_3 (xnor_3_out, in_25, and_3_out);
  xnor xnor_4 (xnor_4_out, in_29, and_4_out);
  xnor xnor_5 (xnor_5_out, and_5_out, in_33);
  xnor xnor_6 (xnor_6_out, and_6_out, in_37);
  xnor xnor_7 (xnor_7_out, in_41, and_7_out);
  xnor xnor_8 (xnor_8_out, in_45, and_8_out);
  xnor xnor_9 (xnor_9_out, and_9_out, in_18);
  xnor xnor_10 (xnor_10_out, and_10_out, in_22);
  xnor xnor_11 (xnor_11_out, in_26, and_11_out);
  xnor xnor_12 (xnor_12_out, in_30, and_12_out);
  xnor xnor_13 (xnor_13_out, and_13_out, in_34);
  xnor xnor_14 (xnor_14_out, and_14_out, in_38);
  xnor xnor_15 (xnor_15_out, in_42, and_15_out);
  xnor xnor_16 (xnor_16_out, in_46, and_16_out);
  xnor xnor_17 (xnor_17_out, and_17_out, in_19);
  xnor xnor_18 (xnor_18_out, and_18_out, in_23);
  xnor xnor_19 (xnor_19_out, in_27, and_19_out);
  xnor xnor_20 (xnor_20_out, in_31, and_20_out);
  xnor xnor_21 (xnor_21_out, and_21_out, in_35);
  xnor xnor_22 (xnor_22_out, and_22_out, in_39);
  xnor xnor_23 (xnor_23_out, in_43, and_23_out);
  xnor xnor_24 (xnor_24_out, in_47, and_24_out);
  xnor xnor_25 (xnor_25_out, and_25_out, in_20);
  xnor xnor_26 (xnor_26_out, and_26_out, in_24);
  xnor xnor_27 (xnor_27_out, in_28, and_27_out);
  xnor xnor_28 (xnor_28_out, in_32, and_28_out);
  xnor xnor_29 (xnor_29_out, and_29_out, in_36);
  xnor xnor_30 (xnor_30_out, and_30_out, in_40);
  xnor xnor_31 (xnor_31_out, in_44, and_31_out);
  xnor xnor_32 (xnor_32_out, in_48, and_32_out);
  and and_33 (and_33_out, xnor_18_out, xnor_17_out, xnor_10_out, xnor_9_out, xnor_1_out, xnor_2_out, xnor_25_out, xnor_26_out, xnor_27_out, xnor_28_out, xnor_3_out, xnor_4_out, xnor_11_out, xnor_12_out, xnor_19_out, xnor_20_out);
  and and_34 (and_34_out, xnor_22_out, xnor_21_out, xnor_14_out, xnor_13_out, xnor_5_out, xnor_6_out, xnor_29_out, xnor_30_out, xnor_31_out, xnor_32_out, xnor_7_out, xnor_8_out, xnor_15_out, xnor_16_out, xnor_23_out, xnor_24_out);
  not not_1 (not_1_out, and_33_out);
  not not_2 (not_2_out, and_34_out);
  and and_35 (and_35_out, and_33_out, and_34_out);
  LED led_65 (.in(and_35_out));
  and and_36 (and_36_out, not_1_out, and_34_out);
  LED led_66 (.in(and_36_out));
  and and_37 (and_37_out, not_2_out, and_33_out);
  LED led_67 (.in(and_37_out));
  and and_38 (and_38_out, not_1_out, not_2_out);
  LED led_68 (.in(and_38_out));

  // Notes on the sheet:
  //   PINS
  //   PINS
  //   INPUT
  //   INPUT
  //   EQ-SUB RECOGNITION (R0)
  //   WEIGHT
  //   WEIGHT
  //   EQ-SUPER RECOGNITION (R1)
  //   OUTPUT
  //   OUTPUT
  //   INTERMEDIATE DECISION-MAKER
  //   INTERMEDIATE DECISION-MAKER
  //   RECOGNIZED
  //   RECOGNIZED
  //   NOT RECOGNIZED
  //   NOT RECOGNIZED
  //   LOGICAL-ANALYZER
  //   EQUIVALENCE
  //   SUPER-PATTERN
  //   SUB-PATTERN
  //   ANTI-PATTERN
endmodule
